// Logisim project alu.circ as structural Verilog: 2 circuits, main circuit ALU
module ALU (
  input  [31:0] X,
  input  [31:0] Y,
  input  [3:0] AluOP,
  output Signed_Overflow,
  output UnSigned_Overflow,
  output Equal,
  output [31:0] Result,
  output [31:0] Result_2
);

  wire adder_1_cout, comparator_1_lt, comparator_4_eq, comparator_5_eq, multiplexer_2_out, or_2_out, sign,
       xnor_1_out, xor_2_out;
  wire [31:0] _7, _8, _9, _10, _11, _12, divider_1_out, divider_1_rem, multiplier_1_cout, multiplier_1_out,
       not_1_out, result_t, shifter_1_out, shifter_2_out, shifter_3_out, y_t;

  // Probe on X
  // Probe on X
  assign not_1_out = ~Y;  // NOT_Gate not_1, 32 bits wide
  // Probe on Y
  // Probe on Y
  Multiplexer #(.width(32)) multiplexer_1 (.in0(Y), .in1(not_1_out), .out(y_t), .sel(AluOP[1]));  // open: en
  assign _7 = X & Y;  // AND_Gate and_1, 32 bits wide
  assign _8 = X | Y;  // OR_Gate or_1, 32 bits wide
  assign _9 = X ^ Y;  // XOR_Gate xor_1, 32 bits wide
  assign _10 = ~(X | Y);  // NOR_Gate nor_1, 32 bits wide
  Comparator #(.width(32)) comparator_1 (.a(X), .b(Y), .lt(comparator_1_lt));  // open: gt, eq
  Comparator #(.width(32), .mode("unsigned")) comparator_2 (.a(X), .b(Y), .lt(sign));  // open: gt, eq
  Comparator #(.width(32)) comparator_3 (.a(X), .b(Y), .eq(Equal));  // open: gt, lt
  Divider #(.width(32)) divider_1 (.a(X), .b(Y), .out(divider_1_out), .rem(divider_1_rem));  // open: upper
  assign _11 = {{31{1'b0}}, comparator_1_lt};  // Bit_Extender bit_extender_1
  assign _12 = {{31{1'b0}}, sign};  // Bit_Extender bit_extender_2
  // Probe on AluOP
  Shifter #(.width(32)) shifter_1 (.in(X), .\dist (Y[4:0]), .out(shifter_1_out));
  Shifter #(.width(32), .shift("ar")) shifter_2 (.in(X), .\dist (Y[4:0]), .out(shifter_2_out));
  Shifter #(.width(32), .shift("lr")) shifter_3 (.in(X), .\dist (Y[4:0]), .out(shifter_3_out));
  Multiplier #(.width(32)) multiplier_1 (.a(X), .b(Y), .out(multiplier_1_out), .cout(multiplier_1_cout));  // open: cin
  Adder #(.width(32)) adder_1 (.a(X), .b(y_t), .out(result_t), .cin(AluOP[1]), .cout(adder_1_cout));
  // Probe on Result
  // Probe on Result
  Comparator #(.width(4)) comparator_4 (.a(AluOP), .b(4'b0101), .eq(comparator_4_eq));  // open: gt, lt
  Comparator #(.width(4)) comparator_5 (.a(AluOP), .b(4'b0110), .eq(comparator_5_eq));  // open: gt, lt
  or or_2 (or_2_out, comparator_4_eq, comparator_5_eq);
  // Probe on Result_2
  Multiplexer multiplexer_2 (.in0(adder_1_cout), .in1(sign), .out(multiplexer_2_out), .sel(AluOP[1]), .en(or_2_out));
  and and_2 (UnSigned_Overflow, multiplexer_2_out, or_2_out);
  xor xor_2 (xor_2_out, result_t[31], X[31]);
  xnor xnor_1 (xnor_1_out, X[31], y_t[31]);
  Multiplexer #(.select(4), .width(32)) multiplexer_3 (
    .in0(shifter_1_out), .in1(shifter_2_out), .in2(shifter_3_out), .in3(multiplier_1_out),
    .in4(divider_1_out), .in5(result_t), .in6(result_t), .in7(_7), .in8(_8), .in9(_9), .in10(_10),
    .in11(_11), .in12(_12), .in13({32{1'b0}}), .in14({32{1'b0}}), .in15({32{1'b0}}), .out(Result), .sel(AluOP));  // open: en
  Multiplexer #(.select(4), .width(32)) multiplexer_4 (
    .in0({32{1'b0}}), .in1({32{1'b0}}), .in2({32{1'b0}}), .in3(multiplier_1_cout), .in4(divider_1_rem),
    .in5({32{1'b0}}), .in6({32{1'b0}}), .in7({32{1'b0}}), .in8({32{1'b0}}), .in9({32{1'b0}}),
    .in10({32{1'b0}}), .in11({32{1'b0}}), .in12({32{1'b0}}), .in13({32{1'b0}}), .in14({32{1'b0}}),
    .in15({32{1'b0}}), .out(Result_2), .sel(AluOP));  // open: en
  and and_3 (Signed_Overflow, or_2_out, xor_2_out, xnor_1_out);

  // Other names for the same wires on the sheet: OF = Signed_Overflow; Result2[31:0] = Result_2; S[3:0] = AluOP;
  //   UOF = UnSigned_Overflow

  // Notes on the sheet:
  //   不要改变此引脚区域内容，也不要改变ALU封装形式
  //   输入引脚
  //   请在下方利用上方输入输出引脚的隧道信号构建ALU电路，ctrl+d复制选择部件
  //   华中科技大学计算机学院 计算机组成原理，鸣谢加州大学伯克利CS61C课程
  //   输出引脚
  //   探测区域
endmodule

module \演示电路  (
  input  [31:0] X,
  input  [31:0] Y,
  input  [3:0] ALUOP,
  output Signed_Overflow,
  output Unsigned_overflow,
  output [31:0] Result,
  output [31:0] Result_2,
  output Equal
);

  // Probe on X
  // Probe on X
  ALU alu_1 (
    .AluOP(ALUOP), .X(X), .Equal(Equal), .Result(Result), .Signed_Overflow(Signed_Overflow), .Y(Y),
    .Result_2(Result_2), .UnSigned_Overflow(Unsigned_overflow));
  // Probe on ALUOP
  // Probe on Y
  // Probe on Y
  // Probe on Result
  // Probe on Result
  // Probe on Result_2
endmodule
