// Logisim project muladd.circ as structural Verilog: 1 circuit, main circuit main
module main (
  input  in_1,
  input  [31:0] \初始 ,
  input  [31:0] \等差 
);

  wire CLK;
  wire [3:0] reg3_q;
  wire [31:0] alu_1_result, alu_2_result, alu_3_result, reg1_q, reg2_q;
  wire [31:4] reg3_q_2;

  Clock clock_1 (.out(CLK));
  // Probe on alu_1_result
  ALU alu_1 (
    .AluOP(4'b0101), .X(\等差 ), .Result(alu_1_result), .Y(reg1_q));  // open: Equal, Signed_Overflow, Result_2, UnSigned_Overflow
  // Probe on reg1_q
  // Probe on \初始 
  Register #(.width(32)) reg1 (.D(alu_1_result), .en(1'b1), .Q(reg1_q), .clk(CLK), .clr(in_1));
  ALU alu_2 (
    .AluOP(4'b0101), .X(\初始 ), .Result(alu_2_result), .Y(reg1_q));  // open: Equal, Signed_Overflow, Result_2, UnSigned_Overflow
  Register #(.width(32)) reg2 (.D(alu_2_result), .en(1'b1), .Q(reg2_q), .clk(CLK), .clr(in_1));
  // Probe on reg2_q
  ALU alu_3 (
    .AluOP(4'b0101), .X(reg2_q), .Result(alu_3_result), .Y({reg3_q_2, reg3_q}));  // open: Equal, Signed_Overflow, Result_2, UnSigned_Overflow
  // Probe on alu_3_result
  Hex_Digit_Display hex_digit_display_1 (.value(reg3_q_2[27:24]));  // open: dp
  Hex_Digit_Display hex_digit_display_2 (.value(reg3_q_2[31:28]));  // open: dp
  Register #(.width(32)) reg3 (.D(alu_3_result), .en(1'b1), .Q({reg3_q_2, reg3_q}), .clk(CLK), .clr(in_1));
  Hex_Digit_Display hex_digit_display_3 (.value(reg3_q_2[23:20]));  // open: dp
  Hex_Digit_Display hex_digit_display_4 (.value(reg3_q_2[19:16]));  // open: dp
  Hex_Digit_Display hex_digit_display_5 (.value(reg3_q_2[11:8]));  // open: dp
  Hex_Digit_Display hex_digit_display_6 (.value(reg3_q_2[15:12]));  // open: dp
  // Probe on {reg3_q_2, reg3_q}
  Hex_Digit_Display hex_digit_display_7 (.value(reg3_q));  // open: dp
  Hex_Digit_Display hex_digit_display_8 (.value(reg3_q_2[7:4]));  // open: dp

  // Other names for the same wires on the sheet: RST = in_1
endmodule
