// Logisim project regfile.circ as structural Verilog
module main (
  input  [4:0] Reg1_num,
  input  [4:0] Reg2,
  input  [4:0] Write_Reg_num,
  input  [31:0] Din,
  input  Write_Enable,
  input  Clock,
  output [31:0] Reg1,
  output [31:0] s0_Value,
  output [31:0] s1_Value,
  output [31:0] s2_Value,
  output [31:0] ra_Value,
  output [31:0] Reg2_2
);

  wire E1, E2, E3, E4, E5, E6, E7, E8, E9, E10, E11, E12, E13, E14, E15, E16, E17, E18, E19, E20, E21, E22,
       E23, E24, E25, E26, E27, E28, E29, E30, E31;
  wire [31:0] I_1, I_2, I_3, I_4, I_5, I_6, I_7, I_8, I_9, I_10, I_11, I_12, I_13, I_14, I_15, I_16, I_17,
       I_18, I_19, I_20, I_21, I_22, I_23, I_24, I_25, I_26, I_27, I_28, I_29, I_30, I_31, O_0, O_1, O_2,
       O_3, O_4, O_5, O_6, O_7, O_8, O_9, O_10, O_11, O_12, O_13, O_14, O_15, O_19, O_20, O_21, O_22, O_23,
       O_24, O_25, O_26, O_27, O_28, O_29, O_30;

  Register #(.width(32)) _0 (.Q(O_0));  // open: D, en, clk, clr
  Register #(.width(32)) _12 (.D(I_12), .en(E12), .Q(O_12), .clk(Clock));  // open: clr
  Register #(.width(32)) _24 (.D(I_24), .en(E24), .Q(O_24), .clk(Clock));  // open: clr
  Register #(.width(32)) _1 (.D(I_1), .en(E1), .Q(O_1), .clk(Clock));  // open: clr
  Register #(.width(32)) _13 (.D(I_13), .en(E13), .Q(O_13), .clk(Clock));  // open: clr
  Register #(.width(32)) _25 (.D(I_25), .en(E25), .Q(O_25), .clk(Clock));  // open: clr
  Register #(.width(32)) _2 (.D(I_2), .en(E2), .Q(O_2), .clk(Clock));  // open: clr
  Register #(.width(32)) _14 (.D(I_14), .en(E14), .Q(O_14), .clk(Clock));  // open: clr
  Register #(.width(32)) _26 (.D(I_26), .en(E26), .Q(O_26), .clk(Clock));  // open: clr
  Multiplexer #(.select(5), .width(32)) multiplexer_1 (
    .in0(O_0), .in1(O_1), .in2(O_2), .in3(O_3), .in4(O_4), .in5(O_5), .in6(O_6), .in7(O_7), .in8(O_8),
    .in9(O_9), .in10(O_10), .in11(O_11), .in12(O_12), .in13(O_13), .in14(O_14), .in15(O_15), .in16(s0_Value),
    .in17(s1_Value), .in18(s2_Value), .in19(O_19), .in20(O_20), .in21(O_21), .in22(O_22), .in23(O_23),
    .in24(O_24), .in25(O_25), .in26(O_26), .in27(O_27), .in28(O_28), .in29(O_29), .in30(O_30),
    .in31(ra_Value), .out(Reg1), .sel(Reg1_num));  // open: en
  Register #(.width(32)) _3 (.D(I_3), .en(E3), .Q(O_3), .clk(Clock));  // open: clr
  Register #(.width(32)) _15 (.D(I_15), .en(E15), .Q(O_15), .clk(Clock));  // open: clr
  Register #(.width(32)) _27 (.D(I_27), .en(E27), .Q(O_27), .clk(Clock));  // open: clr
  Register #(.width(32)) _4 (.D(I_4), .en(E4), .Q(O_4), .clk(Clock));  // open: clr
  Register #(.width(32)) _16 (.D(I_16), .en(E16), .Q(s0_Value), .clk(Clock));  // open: clr
  Register #(.width(32)) _28 (.D(I_28), .en(E28), .Q(O_28), .clk(Clock));  // open: clr
  Register #(.width(32)) _5 (.D(I_5), .en(E5), .Q(O_5), .clk(Clock));  // open: clr
  Register #(.width(32)) _17 (.D(I_17), .en(E17), .Q(s1_Value), .clk(Clock));  // open: clr
  Register #(.width(32)) _29 (.D(I_29), .en(E29), .Q(O_29), .clk(Clock));  // open: clr
  Multiplexer #(.select(5), .width(32)) multiplexer_2 (
    .in0(O_0), .in1(O_1), .in2(O_2), .in3(O_3), .in4(O_4), .in5(O_5), .in6(O_6), .in7(O_7), .in8(O_8),
    .in9(O_9), .in10(O_10), .in11(O_11), .in12(O_12), .in13(O_13), .in14(O_14), .in15(O_15), .in16(s0_Value),
    .in17(s1_Value), .in18(s2_Value), .in19(O_19), .in20(O_20), .in21(O_21), .in22(O_22), .in23(O_23),
    .in24(O_24), .in25(O_25), .in26(O_26), .in27(O_27), .in28(O_28), .in29(O_29), .in30(O_30),
    .in31(ra_Value), .out(Reg2_2), .sel(Reg2));  // open: en
  Register #(.width(32)) _6 (.D(I_6), .en(E6), .Q(O_6), .clk(Clock));  // open: clr
  Register #(.width(32)) _18 (.D(I_18), .en(E18), .Q(s2_Value), .clk(Clock));  // open: clr
  Register #(.width(32)) _30 (.D(I_30), .en(E30), .Q(O_30), .clk(Clock));  // open: clr
  Register #(.width(32)) _7 (.D(I_7), .en(E7), .Q(O_7), .clk(Clock));  // open: clr
  Register #(.width(32)) _19 (.D(I_19), .en(E19), .Q(O_19), .clk(Clock));  // open: clr
  Register #(.width(32)) _31 (.D(I_31), .en(E31), .Q(ra_Value), .clk(Clock));  // open: clr
  Register #(.width(32)) _8 (.D(I_8), .en(E8), .Q(O_8), .clk(Clock));  // open: clr
  Register #(.width(32)) _20 (.D(I_20), .en(E20), .Q(O_20), .clk(Clock));  // open: clr
  Demultiplexer #(.select(5), .width(32)) demultiplexer_1 (
    .out1(I_1), .out2(I_2), .out3(I_3), .out4(I_4), .out5(I_5), .out6(I_6), .out7(I_7), .out8(I_8),
    .out9(I_9), .out10(I_10), .out11(I_11), .out12(I_12), .out13(I_13), .out14(I_14), .out15(I_15),
    .out16(I_16), .out17(I_17), .out18(I_18), .out19(I_19), .out20(I_20), .out21(I_21), .out22(I_22),
    .out23(I_23), .out24(I_24), .out25(I_25), .out26(I_26), .out27(I_27), .out28(I_28), .out29(I_29),
    .out30(I_30), .out31(I_31), .in(Din), .sel(Write_Reg_num), .en(Write_Enable));  // open: out0
  Register #(.width(32)) _9 (.D(I_9), .en(E9), .Q(O_9), .clk(Clock));  // open: clr
  Register #(.width(32)) _21 (.D(I_21), .en(E21), .Q(O_21), .clk(Clock));  // open: clr
  Register #(.width(32)) _10 (.D(I_10), .en(E10), .Q(O_10), .clk(Clock));  // open: clr
  Register #(.width(32)) _22 (.D(I_22), .en(E22), .Q(O_22));  // open: clk, clr
  Register #(.width(32)) _11 (.D(I_11), .en(E11), .Q(O_11), .clk(Clock));  // open: clr
  Register #(.width(32)) _23 (.D(I_23), .en(E23), .Q(O_23), .clk(Clock));  // open: clr
  Demultiplexer #(.select(5), .disabled(0)) demultiplexer_2 (
    .out1(E1), .out2(E2), .out3(E3), .out4(E4), .out5(E5), .out6(E6), .out7(E7), .out8(E8), .out9(E9),
    .out10(E10), .out11(E11), .out12(E12), .out13(E13), .out14(E14), .out15(E15), .out16(E16), .out17(E17),
    .out18(E18), .out19(E19), .out20(E20), .out21(E21), .out22(E22), .out23(E23), .out24(E24), .out25(E25),
    .out26(E26), .out27(E27), .out28(E28), .out29(E29), .out30(E30), .out31(E31), .in(1'b1),
    .sel(Write_Reg_num), .en(Write_Enable));  // open: out0

  // Other names for the same wires on the sheet: clk = Clock; O_16[31:0] = s0_Value; s0[31:0] = s0_Value;
  //   O_17[31:0] = s1_Value; s1[31:0] = s1_Value; O_18[31:0] = s2_Value; s2[31:0] = s2_Value; O_31[31:0] = ra_Value;
  //   ra[31:0] = ra_Value; reg2_num[4:0] = Reg2; reg2_t[31:0] = Reg2_2; WE = Write_Enable; write_data[31:0] = Din

  // Notes on the sheet:
  //   输入引脚
  //   输出引脚
  //   Debug引脚，便于观测寄存器值
  //   请勿修改引脚以及封装，直接使用隧道连接电路
endmodule

module autoalu (
  output [31:0] out_1,
  output [31:0] out_2
);

  wire and_1_out, clock_1_out, comparator_1_eq, not_1_out, or_1_out, or_2_out, register_2_q;
  wire [3:0] alu_1_result_2, alu_1_result_3, alu_1_result_4, alu_1_result_5, alu_1_result_6, main_1_reg1,
       main_1_reg1_3, main_1_reg1_4, main_1_reg1_5, main_1_reg1_6, main_1_reg1_7, main_1_reg1_8;
  wire [4:0] adder_1_out, adder_2_out, counter_2_q;
  wire [5:0] counter_1_q;
  wire [7:4] main_1_reg1_2;
  wire [11:0] alu_1_result;
  wire [31:0] ram_1_data, register_1_q;

  Counter #(.width(6), .max('h3f)) counter_1 (.Q(counter_1_q), .clk(or_1_out));  // open: load, D, count, carry, clr
  Comparator #(.width(6)) comparator_1 (.a(counter_1_q), .b(6'b100000), .eq(comparator_1_eq));  // open: gt, lt
  Clock clock_1 (.out(clock_1_out));
  or or_1 (or_1_out, comparator_1_eq, clock_1_out);
  Counter #(.width(5), .max('h1f)) counter_2 (.Q(counter_2_q), .clk(or_1_out));  // open: load, D, count, carry, clr
  Adder #(.width(5)) adder_1 (.a(5'b00001), .b(counter_2_q), .out(adder_1_out));  // open: cin, cout
  not not_1 (not_1_out, counter_2_q[4]);
  and and_1 (and_1_out, counter_2_q[0], counter_2_q[1], counter_2_q[2], counter_2_q[3], counter_2_q[4]);
  RAM #(.addrWidth(5), .dataWidth(32)) ram_1 (
    .addr(counter_2_q), .data(ram_1_data), .clk(or_1_out), .ld(not_1_out));  // open: sel, clr
  Adder #(.width(5)) adder_2 (.a({1'b0, counter_2_q[3:0]}), .b(5'b00001), .out(adder_2_out));  // open: cin, cout
  assign out_1 = not_1_out ? ram_1_data : 32'bz;  // Controlled_Buffer controlled_buffer_1
  Hex_Digit_Display hex_digit_display_1 (.value(alu_1_result_5));  // open: dp
  Hex_Digit_Display hex_digit_display_2 (.value(alu_1_result_6));  // open: dp
  Register #(.width(32)) register_1 (
    .D({alu_1_result_6, alu_1_result_5, alu_1_result_4, alu_1_result_3, alu_1_result_2, alu_1_result}),
    .Q(register_1_q), .clk(or_1_out), .clr(and_1_out));  // open: en
  Hex_Digit_Display hex_digit_display_3 (.value(alu_1_result_3));  // open: dp
  Hex_Digit_Display hex_digit_display_4 (.value(alu_1_result_4));  // open: dp
  ALU alu_1 (
    .AluOP(4'b0101), .X(out_1),
    .Result({alu_1_result_6, alu_1_result_5, alu_1_result_4, alu_1_result_3, alu_1_result_2, alu_1_result}),
    .Y(register_1_q));  // open: Equal, Signed_Overflow, Result_2, UnSigned_Overflow
  Register #(.width(1)) register_2 (.D(counter_2_q[4]), .Q(register_2_q), .clk(or_1_out));  // open: en, clr
  Hex_Digit_Display hex_digit_display_5 (.value(alu_1_result_2));  // open: dp
  assign ram_1_data = or_2_out ? out_2 : 32'bz;  // Controlled_Buffer controlled_buffer_2
  or or_2 (or_2_out, counter_2_q[4], register_2_q);
  Hex_Digit_Display hex_digit_display_6 (.value(alu_1_result[11:8]));  // open: dp
  Hex_Digit_Display hex_digit_display_7 (.value(alu_1_result[7:4]));  // open: dp
  assign out_2 = or_2_out ? {main_1_reg1_8, main_1_reg1_7, main_1_reg1_6, main_1_reg1_5, main_1_reg1_4, main_1_reg1_3, main_1_reg1_2, main_1_reg1} : 32'bz;  // Controlled_Buffer controlled_buffer_3
  Hex_Digit_Display hex_digit_display_8 (.value(alu_1_result[3:0]));  // open: dp
  Hex_Digit_Display hex_digit_display_9 (.value(main_1_reg1_8));  // open: dp
  main main_1 (
    .Reg1_num(adder_2_out), .Write_Reg_num(adder_1_out),
    .Din({alu_1_result_6, alu_1_result_5, alu_1_result_4, alu_1_result_3, alu_1_result_2, alu_1_result}),
    .Write_Enable(1'b1), .Clock(or_1_out),
    .Reg1({main_1_reg1_8, main_1_reg1_7, main_1_reg1_6, main_1_reg1_5, main_1_reg1_4, main_1_reg1_3, main_1_reg1_2, main_1_reg1}));  // open: Reg2, Reg2_2, s0_Value, s1_Value, s2_Value, ra_Value
  Hex_Digit_Display hex_digit_display_10 (.value(main_1_reg1_6));  // open: dp
  Hex_Digit_Display hex_digit_display_11 (.value(main_1_reg1_7));  // open: dp
  Hex_Digit_Display hex_digit_display_12 (.value(main_1_reg1_5));  // open: dp
  Hex_Digit_Display hex_digit_display_13 (.value(main_1_reg1_3));  // open: dp
  Hex_Digit_Display hex_digit_display_14 (.value(main_1_reg1_4));  // open: dp
  Hex_Digit_Display hex_digit_display_15 (.value(main_1_reg1_2));  // open: dp
  Hex_Digit_Display hex_digit_display_16 (.value(main_1_reg1));  // open: dp

  // Other names for the same wires on the sheet: 出数据[31:0] = out_1; 记录数据[31:0] = out_2
endmodule

module autoalu_x (
);

  wire and_1_out, clk, comparator_1_eq, counter_3_carry, not_2_out, ram_read, ram_write;
  wire [3:0] main_1_reg1_2, ram_1_data_2, ram_1_data_3, ram_1_data_4, ram_1_data_5, ram_1_data_6;
  wire [4:0] adder_1_out, counter_1_q, counter_2_q, multiplexer_1_out;
  wire [7:0] counter_4_q;
  wire [11:0] ram_1_data;
  wire [31:0] alu_1_result, main_1_reg1;

  Clock clock_1 (.out(clk));
  Counter #(.width(5), .max('h1f)) counter_1 (.Q(counter_1_q), .clk(ram_write));  // open: load, D, count, carry, clr
  Counter #(.width(5), .max('h1f)) counter_2 (.Q(counter_2_q), .clk(ram_write));  // open: load, D, count, carry, clr
  Counter #(.width(1), .max('h1)) counter_3 (
    .count(not_2_out), .Q(ram_write), .carry(counter_3_carry), .clk(clk));  // open: load, D, clr
  Adder #(.width(5)) adder_1 (.a(counter_2_q), .b(5'b01111), .out(adder_1_out));  // open: cin, cout
  Counter counter_4 (.Q(counter_4_q), .clk(counter_3_carry));  // open: load, D, count, carry, clr
  Hex_Digit_Display hex_digit_display_1 (.value(ram_1_data_6));  // open: dp
  Hex_Digit_Display hex_digit_display_2 (.value(ram_1_data_5));  // open: dp
  Multiplexer #(.width(5)) multiplexer_1 (
    .in0(counter_1_q), .in1(adder_1_out), .out(multiplexer_1_out), .sel(ram_write));  // open: en
  not not_1 (ram_read, ram_write);
  Hex_Digit_Display hex_digit_display_3 (.value(ram_1_data_4));  // open: dp
  Hex_Digit_Display hex_digit_display_4 (.value(ram_1_data_3));  // open: dp
  Comparator comparator_1 (.a(counter_4_q), .b(8'h10), .eq(comparator_1_eq));  // open: gt, lt
  not not_2 (not_2_out, comparator_1_eq);
  Hex_Digit_Display hex_digit_display_5 (.value(ram_1_data_2));  // open: dp
  RAM #(.addrWidth(5), .dataWidth(32), .bus("separate")) ram_1 (
    .addr(multiplexer_1_out), .din({main_1_reg1[31:8], main_1_reg1_2, main_1_reg1[3:0]}),
    .data({ram_1_data_6, ram_1_data_5, ram_1_data_4, ram_1_data_3, ram_1_data_2, ram_1_data}),
    .str(ram_write), .clk(clk), .ld(ram_read));  // open: sel, clr
  and and_1 (and_1_out, ram_read, not_2_out);
  Hex_Digit_Display hex_digit_display_6 (.value(ram_1_data[7:4]));  // open: dp
  Hex_Digit_Display hex_digit_display_7 (.value(ram_1_data[11:8]));  // open: dp
  main main_1 (
    .Reg1_num(5'b00001), .Write_Reg_num(5'b00001), .Din(alu_1_result), .Write_Enable(and_1_out), .Clock(clk),
    .Reg1({main_1_reg1[31:8], main_1_reg1_2, main_1_reg1[3:0]}));  // open: Reg2, Reg2_2, s0_Value, s1_Value, s2_Value, ra_Value
  Hex_Digit_Display hex_digit_display_8 (.value(ram_1_data[3:0]));  // open: dp
  Hex_Digit_Display hex_digit_display_9 (.value(main_1_reg1[31:28]));  // open: dp
  Hex_Digit_Display hex_digit_display_10 (.value(main_1_reg1[27:24]));  // open: dp
  ALU alu_1 (
    .AluOP(4'b0101), .X({ram_1_data_6, ram_1_data_5, ram_1_data_4, ram_1_data_3, ram_1_data_2, ram_1_data}),
    .Result(alu_1_result), .Y({main_1_reg1[31:8], main_1_reg1_2, main_1_reg1[3:0]}));  // open: Equal, Signed_Overflow, Result_2, UnSigned_Overflow
  Hex_Digit_Display hex_digit_display_11 (.value(main_1_reg1[19:16]));  // open: dp
  Hex_Digit_Display hex_digit_display_12 (.value(main_1_reg1[23:20]));  // open: dp
  Hex_Digit_Display hex_digit_display_13 (.value(main_1_reg1[15:12]));  // open: dp
  Hex_Digit_Display hex_digit_display_14 (.value(main_1_reg1_2));  // open: dp
  Hex_Digit_Display hex_digit_display_15 (.value(main_1_reg1[11:8]));  // open: dp
  Hex_Digit_Display hex_digit_display_16 (.value(main_1_reg1[3:0]));  // open: dp
endmodule
