// Logisim project 薛成玺cpu.circ as structural Verilog: 3 circuits, main circuit main
module main (
);

  wire ALUop, ALUSrc, and_1_out, Bne, Branch, CLK, clock_1_out, equal, Jump, Load, MemtoReg, RegDst,
       RegWrite, Store, SYSCALL, xor_1_out;
  wire [1:0] alu_1_result;
  wire [3:0] alu_1_result_3, alu_1_result_4, alu_1_result_5, alu_1_result_6, alu_1_result_7, alucontrol_1_op;
  wire [4:0] multiplexer_1_out;
  wire [9:0] alu_1_result_2;
  wire [25:0] shifter_1_out;
  wire [31:0] adder_1_out, adder_2_out, bit_extender_1_out, counter_1_q, goback1, main_1_reg1, main_1_reg2_2,
       multiplexer_2_out, multiplexer_3_out, multiplexer_5_out, PC_q, ram_1_data, rom_1_data, shifter_2_out;

  Clock clock_1 (.out(clock_1_out));
  Register #(.width(32)) PC (.D(goback1), .Q(PC_q), .clk(CLK));  // open: en, clr
  Counter #(.width(32), .max('hffffffff)) counter_1 (.Q(counter_1_q), .clk(CLK));  // open: load, D, count, carry, clr
  or or_1 (CLK, clock_1_out, SYSCALL);
  // Probe on counter_1_q
  Adder #(.width(32)) adder_1 (.a(32'h4), .b(PC_q), .out(adder_1_out));  // open: cin, cout
  // Probe on rom_1_data
  ROM #(.addrWidth(10), .dataWidth(32)) rom_1 (.addr(PC_q[11:2]), .data(rom_1_data));  // open: sel
  Shifter #(.width(26)) shifter_1 (.in(rom_1_data[25:0]), .\dist (5'b00010), .out(shifter_1_out));
  control control (
    .BIT0(rom_1_data[31]), .BIT1(rom_1_data[30]), .BIT2(rom_1_data[29]), .BIT3(rom_1_data[28]),
    .BIT4(rom_1_data[27]), .BIT5(rom_1_data[26]), .MemRead(Load), .MemWrite(Store), .ALUSrc(ALUSrc),
    .ALUop(ALUop), .Jump(Jump), .MemtoReg(MemtoReg), .Branch(Branch), .RegDst(RegDst), .RegWrite(RegWrite),
    .Bne(Bne));
  Multiplexer #(.width(5), .enable("false")) multiplexer_1 (
    .in0(rom_1_data[20:16]), .in1(rom_1_data[15:11]), .out(multiplexer_1_out), .sel(RegDst));
  assign bit_extender_1_out = {{16{rom_1_data[15]}}, rom_1_data[15:0]};  // Bit_Extender bit_extender_1
  regfile_main main_1 (
    .Reg1_num(rom_1_data[25:21]), .Reg2(rom_1_data[20:16]), .Write_Reg_num(multiplexer_1_out),
    .Din(multiplexer_5_out), .Write_Enable(RegWrite), .Clock(CLK), .Reg1(main_1_reg1), .Reg2_2(main_1_reg2_2));  // open: s0_Value, s1_Value, s2_Value, ra_Value
  Shifter #(.width(32)) shifter_2 (.in(bit_extender_1_out), .\dist (5'b00010), .out(shifter_2_out));
  Multiplexer #(.width(32), .enable("false")) multiplexer_2 (
    .in0(main_1_reg2_2), .in1(bit_extender_1_out), .out(multiplexer_2_out), .sel(ALUSrc));
  alucontrol alucontrol_1 (.OP(alucontrol_1_op), .SYSCALL(SYSCALL), .Operation(rom_1_data[5:0]), .ALUop(ALUop));
  Adder #(.width(32)) adder_2 (.a(adder_1_out), .b(shifter_2_out), .out(adder_2_out));  // open: cin, cout
  xor xor_1 (xor_1_out, Bne, equal);
  ALU alu_1 (
    .AluOP(alucontrol_1_op), .X(main_1_reg1), .Equal(equal),
    .Result({alu_1_result_7, alu_1_result_6, alu_1_result_5, alu_1_result_4, alu_1_result_3, alu_1_result_2, alu_1_result}),
    .Y(multiplexer_2_out));  // open: Signed_Overflow, Result_2, UnSigned_Overflow
  Multiplexer #(.width(32), .enable("false")) multiplexer_3 (
    .in0(adder_1_out), .in1(adder_2_out), .out(multiplexer_3_out), .sel(and_1_out));
  and and_1 (and_1_out, Branch, xor_1_out);
  Multiplexer #(.width(32), .enable("false")) multiplexer_4 (
    .in0({adder_1_out[31:28], shifter_1_out, 2'b00}), .in1(multiplexer_3_out), .out(goback1), .sel(Jump));
  Hex_Digit_Display hex_digit_display_1 (.value(alu_1_result_3));  // open: dp
  Hex_Digit_Display hex_digit_display_2 (.value(alu_1_result_7));  // open: dp
  Hex_Digit_Display hex_digit_display_3 (.value(alu_1_result_2[9:6]));  // open: dp
  Hex_Digit_Display hex_digit_display_4 (.value(alu_1_result_2[5:2]));  // open: dp
  Hex_Digit_Display hex_digit_display_5 (.value(alu_1_result_5));  // open: dp
  Hex_Digit_Display hex_digit_display_6 (.value(alu_1_result_6));  // open: dp
  RAM #(.addrWidth(10), .dataWidth(32), .bus("separate")) ram_1 (
    .addr(alu_1_result_2), .din(main_1_reg2_2), .data(ram_1_data), .str(Store), .clk(CLK), .ld(Load));  // open: sel, clr
  Hex_Digit_Display hex_digit_display_7 (.value({alu_1_result_2[1:0], alu_1_result}));  // open: dp
  Hex_Digit_Display hex_digit_display_8 (.value(alu_1_result_4));  // open: dp
  Multiplexer #(.width(32), .enable("false")) multiplexer_5 (
    .in0({alu_1_result_7, alu_1_result_6, alu_1_result_5, alu_1_result_4, alu_1_result_3, alu_1_result_2, alu_1_result}),
    .in1(ram_1_data), .out(multiplexer_5_out), .sel(MemtoReg));

  // Notes on the sheet:
  //   contents of rom_1 (hex, n*v repeats v):
  //   2010ffff 20110000 ae300000 22100001 22310004 ae300000 22100001 22310004 ae300000 22100001 22310004
  //   ae300000 22100001 22310004 ae300000 22100001 22310004 ae300000 22100001 22310004 ae300000 22100001
  //   22310004 ae300000 22100001 22310004 ae300000 22100001 22310004 ae300000 22100001 22310004 ae300000
  //   22100001 22310004 ae300000 22100001 22310004 ae300000 22100001 22310004 ae300000 22100001 22310004
  //   ae300000 22100001 22310004 ae300000 22100001 22310004 22100001 8020 2011003c 8e130000 8e340000
  //   274402a 11000002 ae330000 ae140000 2231fffc 1611fff8 22100004 2011003c 1611fff5 2002000a c
endmodule

module control (
  input  BIT0,
  input  BIT1,
  input  BIT2,
  input  BIT3,
  input  BIT4,
  input  BIT5,
  output MemRead,
  output MemWrite,
  output ALUSrc,
  output ALUop,
  output Jump,
  output MemtoReg,
  output Branch,
  output RegDst,
  output RegWrite,
  output Bne
);

  wire and_6_out, and_7_out, not_1_out, not_2_out, not_3_out, not_4_out, not_5_out, not_6_out, not_7_out,
       not_8_out, not_9_out, not_10_out, not_11_out, not_12_out, not_13_out;

  not not_1 (not_1_out, BIT2);
  not not_2 (not_2_out, BIT2);
  not not_3 (not_3_out, BIT3);
  not not_4 (not_4_out, BIT4);
  and and_1 (MemRead, BIT0, not_1_out);
  or or_1 (ALUSrc, BIT4, BIT2);
  not not_5 (not_5_out, BIT2);
  not not_6 (not_6_out, BIT2);
  not not_7 (not_7_out, BIT3);
  not not_8 (not_8_out, BIT4);
  not not_9 (not_9_out, BIT2);
  not not_10 (not_10_out, BIT3);
  not not_11 (not_11_out, BIT3);
  not not_12 (not_12_out, BIT4);
  not not_13 (not_13_out, BIT4);
  and and_2 (MemWrite, BIT0, BIT2);
  and and_3 (ALUop, not_2_out, not_3_out, not_4_out);
  and and_4 (MemtoReg, BIT0, not_5_out);
  and and_5 (RegDst, not_6_out, not_7_out, not_8_out);
  and and_6 (and_6_out, not_9_out, not_10_out);
  and and_7 (and_7_out, not_11_out, not_12_out);
  and and_8 (Bne, not_13_out, BIT5);
  or or_2 (RegWrite, and_6_out, and_7_out);

  assign Branch = BIT3;
  assign Jump = 1'b1;
endmodule

module alucontrol (
  input  ALUop,
  input  [5:0] Operation,
  output [3:0] OP,
  output SYSCALL
);

  wire not_1_out, not_2_out, not_3_out, not_4_out;
  wire [3:0] multiplexer_1_out, multiplexer_2_out;

  Multiplexer #(.width(4), .disabled(0), .enable("false")) multiplexer_1 (
    .in0(4'b0101), .in1(4'b1011), .out(multiplexer_1_out), .sel(Operation[1]));
  Multiplexer #(.width(4), .disabled(0), .enable("false")) multiplexer_2 (
    .in0(4'b0000), .in1(multiplexer_1_out), .out(multiplexer_2_out), .sel(Operation[5]));
  Multiplexer #(.width(4), .disabled(0), .enable("false")) multiplexer_3 (
    .in0(4'b0101), .in1(multiplexer_2_out), .out(OP), .sel(ALUop));
  not not_1 (not_1_out, Operation[0]);
  not not_2 (not_2_out, Operation[4]);
  not not_3 (not_3_out, Operation[1]);
  not not_4 (not_4_out, Operation[5]);
  and and_1 (SYSCALL, ALUop, not_1_out, not_3_out, Operation[2], Operation[3], not_2_out, not_4_out);
endmodule
